# Fritzing sketch masa_lambasi_kontrol (saved by Fritzing 0.9.3b)
breadboards: 1

parts:
  Parça1 = Arduino Uno (Rev3)
  Parça2 = Bluetooth HC-05 Macho  # not connected
  LED1 = LED - 5mm [color="Red (633nm)" package="5 mm [THT]"]
  LED2 = LED - 5mm [color="Red (633nm)" package="5 mm [THT]"]
  LED3 = LED - 5mm [color="Red (633nm)" package="5 mm [THT]"]
  R1 = Rotary Potentiometer (Small) [maximum_resistance=100kΩ package=THT]  # not connected
  S1 = Pushbutton [package="[THT]"]
  R2 = Resistor [tolerance=±5% resistance=220 package=THT]
  R3 = Resistor [tolerance=±5% resistance=220 package=THT]
  R4 = Resistor [tolerance=±5% resistance=220 package=THT]

nets:
  N1: Parça1.D8, R2.Pin_0
  N2: Parça1.D9_PWM, R3.Pin_0
  N3: Parça1.D10_PWM/SS, R4.Pin_0
  N4: Parça1.GND, LED1.anode, LED2.anode, LED3.anode, R2.Pin_1
  N5: LED2.cathode, R3.Pin_1
  N6: LED3.cathode, R4.Pin_1
  N7: S1.Pin_1, S1.Pin_2
  N8: S1.Pin_3, S1.Pin_4
